# Fritzing sketch Brain Machine Schematic (saved by Fritzing 0.9.3b)

parts:
  Part1 = Arduino Uno (Rev3)
  SP1 = SPEAKER [package=pcb_mount_speaker]
  SP2 = SPEAKER [package=pcb_mount_speaker]
  LED1 = LEDs [package=led10mm]
  LED2 = LEDs [package=led10mm]
  U1 = POT_SWITCH [package=pot_pth]
  S1 = Toggle Switch [package=THT]
  BAT1 = BC9VPC [package=bc9vpc]
  R1 = Resistor [tolerance=±5% resistance=220 package="2010 [SMD]"]
  Power_plug1 = Power plug

nets:
  N1: Part1.D9_PWM, SP1.-
  N2: Part1.D10_PWM/SS, SP2.-
  N3: Part1.D11_PWM/MOSI, LED2.A
  N4: Part1.D13/SCK, LED1.A
  N5: Part1.GND, LED1.C, LED2.C, U1.G$2_1, S1.L1, R1.Pin_1
  N6: Part1.D2, R1.Pin_0
  N7: Part1.VIN, S1.COM
  N8: SP1.+, U1.G$1_A
  N9: SP2.+, U1.G$1_E
  N10: BAT1.V+, Power_plug1.VCC
  N11: BAT1.V-, Power_plug1.GND
