# Fritzing sketch EEG Amplifier with sensors (saved by Fritzing 0.9.3b)
breadboards: 1

parts:
  Part1 = Arduino Uno (Rev3)
  C1 = Capacitor Polarized [package=cpol-radial-1000uf-25v]
  Q1 = NPN-Transistor [package="TO92 [THT]"]
  R1 = Resistor [tolerance=±5% resistance=220 package="0603 [SMD]"]
  R2 = Resistor [tolerance=±5% resistance=220 package="0603 [SMD]"]
  EEG_Ground_sensor_to_ear = TOUCH [package=touch1]
  EEG_Active_sensor_to_head = TOUCH [package=touch1]

nets:
  N1: Part1.A1, R2.Pin_0
  N2: Part1.GND, C1.+, R1.Pin_1, EEG_Ground_sensor_to_ear.T2, EEG_Active_sensor_to_head.T2
  N3: C1.-, Q1.E
  N4: Q1.B, R1.Pin_0
  N5: Q1.C, R2.Pin_1
